# Fritzing sketch 1_pix_camera (saved by Fritzing 0.9.6b)
breadboards: 1

parts:
  OLED1 = OLED 128x64 I2C Monochrome Display
  R1 = Photocell (LDR) [package=THT]
  R2 = Resistor [tolerance=±5% resistance=10k package="0603 [SMD]"]
  esp1 = ESP32 DevKitc V4

nets:
  N1: OLED1.GND, R1.pin_1, esp1.GND#12
  N2: OLED1.VDD, esp1.EN
  N3: OLED1.SCK, esp1.IO22
  N4: OLED1.SDA, esp1.IO21
  N5: R1.pin_0, R2.Pin_1, esp1.IO2
  N6: R2.Pin_0, esp1.3V3

custom parts:
  ESP32 DevKitc V4: ESP32-DevKitC board with ESP32-WROOM-32 module. ESP32-DevKitC V4 is a small-sized ESP32-based development board produced by Espressif. Most of the pins on the ESP module are broken out to the pin headers on the board. The pins D0, D1, D2, D3, CMD and CLK are used internally for communication between ESP32 and SPI flash memory. They are grouped on both sides near the USB connector. Avoid using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
